// Logisim project All_Flip_Flop.circ as structural Verilog: 1 circuit, main circuit main
module main (
  input  in_1,
  input  S_for_NAND_SR_FlipFlop,
  input  in_3,
  input  K,
  input  J,
  input  R_for_NAND_SR_FlipFlop,
  input  S,
  input  J_FF,
  input  R,
  input  K_FF,
  output out_11,
  output out_12,
  output out_13,
  output Q_for_NAND_SR_FlipFlop,
  output out_15,
  output out_16,
  output out_17,
  output Q_bar_for_NAND_SR_FlipFlop,
  output out_19,
  output out_20,
  output out_21,
  output out_22
);

  wire and_1_out, and_2_out, and_3_out, and_4_out, clock_1_out, clock_2_out, clock_3_out, clock_4_out,
       clock_5_out, Clock_for_NAND_SR_FlipFlop_out, nand_1_out, nand_2_out, nand_3_out, nand_4_out,
       nand_7_out, nand_8_out, nand_9_out, nand_10_out, nand_13_out, nand_14_out, nand_15_out, nand_16_out,
       nand_17_out, nand_18_out, nand_21_out, nand_22_out, not_1_out, not_2_out, not_3_out;

  Clock clock_1 (.out(clock_1_out));
  Clock Clock_for_NAND_SR_FlipFlop (.out(Clock_for_NAND_SR_FlipFlop_out));
  nand nand_1 (nand_1_out, S_for_NAND_SR_FlipFlop, Clock_for_NAND_SR_FlipFlop_out);
  nand nand_2 (nand_2_out, Clock_for_NAND_SR_FlipFlop_out, R_for_NAND_SR_FlipFlop);
  nand nand_3 (nand_3_out, S, clock_1_out);
  nand nand_4 (nand_4_out, clock_1_out, R);
  nand nand_5 (Q_for_NAND_SR_FlipFlop, nand_1_out, Q_bar_for_NAND_SR_FlipFlop);
  nand nand_6 (Q_bar_for_NAND_SR_FlipFlop, Q_for_NAND_SR_FlipFlop, nand_2_out);
  nand nand_7 (nand_7_out, nand_3_out, nand_8_out);
  nand nand_8 (nand_8_out, nand_7_out, nand_4_out);
  not not_1 (not_1_out, clock_1_out);
  nand nand_9 (nand_9_out, nand_7_out, not_1_out);
  nand nand_10 (nand_10_out, not_1_out, nand_8_out);
  Clock clock_2 (.out(clock_2_out));
  nand nand_11 (out_19, nand_9_out, out_21);
  nand nand_12 (out_21, out_19, nand_10_out);
  and and_1 (and_1_out, out_13, K, clock_2_out);
  and and_2 (and_2_out, clock_2_out, J, out_17);
  Clock clock_3 (.out(clock_3_out));
  nor nor_1 (out_13, and_1_out, out_17);
  nor nor_2 (out_17, out_13, and_2_out);
  nand nand_13 (nand_13_out, out_22, J_FF, clock_3_out);
  nand nand_14 (nand_14_out, clock_3_out, K_FF, out_20);
  Clock clock_4 (.out(clock_4_out));
  not not_2 (not_2_out, in_1);
  nand nand_15 (nand_15_out, nand_13_out, nand_16_out);
  nand nand_16 (nand_16_out, nand_15_out, nand_14_out);
  nand nand_17 (nand_17_out, in_1, clock_4_out);
  nand nand_18 (nand_18_out, clock_4_out, not_2_out);
  not not_3 (not_3_out, clock_3_out);
  nand nand_19 (out_11, nand_17_out, out_15);
  nand nand_20 (out_15, out_11, nand_18_out);
  nand nand_21 (nand_21_out, nand_15_out, not_3_out);
  nand nand_22 (nand_22_out, not_3_out, nand_16_out);
  Clock clock_5 (.out(clock_5_out));
  nand nand_23 (out_20, nand_21_out, out_22);
  nand nand_24 (out_22, out_20, nand_22_out);
  and and_3 (and_3_out, out_12, in_3, clock_5_out);
  and and_4 (and_4_out, clock_5_out, in_3, out_16);
  nor nor_3 (out_12, and_3_out, out_16);
  nor nor_4 (out_16, out_12, and_4_out);

  // Notes on the sheet:
  //   SR FlipFlop Using NAND
  //   Master Slave SR FlipFlop Using NAND
  //   JK FlipFlop Using NOR
  //   Master Slave JK FlipFlop Using NAND
  //   D FlipFlop Using NAND
  //   T FlipFlop Using NOR
endmodule
