// Logisim project CS240_PROJECT_KHELAWAN_VIDASH.circ as structural Verilog
module Half_Adder (
  input  in_1,
  input  in_2,
  output out_3,
  output out_4
);

  and and_1 (out_4, in_1, in_2);
  xor xor_1 (out_3, in_1, in_2);
endmodule

module Full_Adder (
  input  in_1,
  input  in_2,
  input  in_3,
  output out_4,
  output out_5
);

  wire and_1_out, and_2_out, xor_1_out;

  xor xor_1 (xor_1_out, in_1, in_2);
  and and_1 (and_1_out, xor_1_out, in_3);
  and and_2 (and_2_out, in_1, in_2);
  xor xor_2 (out_4, xor_1_out, in_3);
  or or_1 (out_5, and_1_out, and_2_out);
endmodule

module _4BitInverter (
  input  A1,
  input  A2,
  input  in_3,
  input  A4,
  input  C,
  output out_6,
  output out_7,
  output out_8,
  output out_9
);

  wire Half_Adder_2_out_3, Half_Adder_3_out_3, Half_Adder_out_3, xor_1_out, xor_2_out, xor_3_out, xor_4_out;

  xor xor_1 (xor_1_out, A1, C);
  Half_Adder Half_Adder (.in_1(xor_1_out), .in_2(C), .out_3(Half_Adder_out_3), .out_4(out_6));
  xor xor_2 (xor_2_out, A2, C);
  Half_Adder Half_Adder_2 (.in_1(xor_2_out), .in_2(Half_Adder_out_3), .out_3(Half_Adder_2_out_3), .out_4(out_7));
  xor xor_3 (xor_3_out, in_3, C);
  Half_Adder Half_Adder_3 (.in_1(xor_3_out), .in_2(Half_Adder_2_out_3), .out_3(Half_Adder_3_out_3), .out_4(out_8));
  xor xor_4 (xor_4_out, A4, C);
  Half_Adder Half_Adder_4 (.in_1(xor_4_out), .in_2(Half_Adder_3_out_3), .out_4(out_9));  // open: out_3
endmodule

module _8BitInverter (
  input  A1,
  input  A2,
  input  A3,
  input  A4,
  input  A5,
  input  A6,
  input  A7,
  input  A8,
  input  C,
  output out_10,
  output out_11,
  output out_12,
  output out_13,
  output out_14,
  output out_15,
  output out_16,
  output out_17
);

  wire Half_Adder_2_out_3, Half_Adder_3_out_3, Half_Adder_4_out_3, Half_Adder_5_out_3, Half_Adder_6_out_3,
       Half_Adder_7_out_3, Half_Adder_8_out_3, Half_Adder_out_3, xor_1_out, xor_2_out, xor_3_out, xor_4_out,
       xor_5_out, xor_6_out, xor_7_out, xor_8_out;

  xor xor_1 (xor_1_out, C, A1);
  xor xor_2 (xor_2_out, C, A2);
  xor xor_3 (xor_3_out, C, A3);
  xor xor_4 (xor_4_out, C, A4);
  xor xor_5 (xor_5_out, C, A5);
  xor xor_6 (xor_6_out, C, A6);
  xor xor_7 (xor_7_out, C, A7);
  xor xor_8 (xor_8_out, C, A8);
  Half_Adder Half_Adder (.in_1(xor_1_out), .in_2(Half_Adder_2_out_3), .out_3(Half_Adder_out_3), .out_4(out_10));
  Half_Adder Half_Adder_2 (.in_1(xor_2_out), .in_2(Half_Adder_3_out_3), .out_3(Half_Adder_2_out_3), .out_4(out_11));
  Half_Adder Half_Adder_3 (.in_1(xor_3_out), .in_2(Half_Adder_4_out_3), .out_3(Half_Adder_3_out_3), .out_4(out_12));
  Half_Adder Half_Adder_4 (.in_1(xor_4_out), .in_2(Half_Adder_5_out_3), .out_3(Half_Adder_4_out_3), .out_4(out_13));
  Half_Adder Half_Adder_5 (.in_1(xor_5_out), .in_2(Half_Adder_6_out_3), .out_3(Half_Adder_5_out_3), .out_4(out_14));
  Half_Adder Half_Adder_6 (.in_1(xor_6_out), .in_2(Half_Adder_7_out_3), .out_3(Half_Adder_6_out_3), .out_4(out_15));
  Half_Adder Half_Adder_7 (.in_1(xor_7_out), .in_2(Half_Adder_8_out_3), .out_3(Half_Adder_7_out_3), .out_4(out_16));
  Half_Adder Half_Adder_8 (.in_1(xor_8_out), .in_2(C), .out_3(Half_Adder_8_out_3), .out_4(out_17));
endmodule

// 4 Bit Adder
module _4BitAdder (
  input  A1,
  input  B1,
  input  A2,
  input  B2,
  input  A3,
  input  B3,
  input  A4,
  input  B4,
  output out_9,
  output out_10,
  output out_11,
  output out_12,
  output out_13
);

  wire full_adder_1_out_4, full_adder_2_out_4, full_adder_3_out_4;

  Full_Adder full_adder_1 (.in_1(B1), .in_2(A1), .in_3(1'b0), .out_4(full_adder_1_out_4), .out_5(out_10));
  Full_Adder full_adder_2 (.in_1(B2), .in_2(A2), .in_3(full_adder_1_out_4), .out_4(full_adder_2_out_4), .out_5(out_11));
  Full_Adder full_adder_3 (.in_1(B3), .in_2(A3), .in_3(full_adder_2_out_4), .out_4(full_adder_3_out_4), .out_5(out_12));
  Full_Adder full_adder_4 (.in_1(B4), .in_2(A4), .in_3(full_adder_3_out_4), .out_4(out_9), .out_5(out_13));

  // Notes on the sheet:
  //   Ground / Can also use a Carry
endmodule

module UnsignedMultiplier (
  input  B1,
  input  B2,
  input  B3,
  input  B4,
  input  A1,
  input  C1,
  input  A2,
  input  in_8,
  input  C2,
  input  A3,
  input  C3,
  input  A4,
  output out_13,
  output out_14,
  output out_15,
  output out_16,
  output out_17,
  output out_18,
  output out_19,
  output out_20
);

  wire _4Bit_Adder_out_10, _4Bit_Adder_out_11, _4Bit_Adder_out_12, _4Bit_Adder_out_13, and_1_out, and_2_out,
       and_3_out, and_4_out, and_5_out, and_6_out, and_7_out, and_8_out, and_9_out, and_10_out, and_11_out,
       and_12_out, and_13_out, and_14_out, and_15_out, n4bitadder_1_out_10, n4bitadder_1_out_11,
       n4bitadder_1_out_12, n4bitadder_1_out_13;

  and and_1 (and_1_out, A2, B1);
  and and_2 (and_2_out, A3, B1);
  and and_3 (and_3_out, A4, B2);
  and and_4 (and_4_out, A4, B1);
  and and_5 (and_5_out, A2, B2);
  and and_6 (and_6_out, A3, B2);
  and and_7 (and_7_out, A4, B3);
  and and_8 (and_8_out, A2, B3);
  and and_9 (and_9_out, A3, B3);
  and and_10 (and_10_out, A3, C2);
  and and_11 (and_11_out, A4, C3);
  and and_12 (and_12_out, A2, C1);
  _4BitAdder _4Bit_Adder (
    .A1(and_1_out), .B1(and_5_out), .A2(and_8_out), .B2(and_12_out), .A3(in_8), .B3(and_13_out),
    .A4(and_14_out), .B4(and_15_out), .out_10(_4Bit_Adder_out_10), .out_11(_4Bit_Adder_out_11),
    .out_12(_4Bit_Adder_out_12), .out_13(_4Bit_Adder_out_13), .out_9(out_20));
  _4BitAdder u_4bitadder_1 (
    .A1(and_2_out), .B1(and_6_out), .A2(and_9_out), .B2(and_10_out), .A3(_4Bit_Adder_out_10),
    .B3(_4Bit_Adder_out_11), .A4(_4Bit_Adder_out_12), .B4(_4Bit_Adder_out_13), .out_10(n4bitadder_1_out_10),
    .out_11(n4bitadder_1_out_11), .out_12(n4bitadder_1_out_12), .out_13(n4bitadder_1_out_13), .out_9(out_19));
  _4BitAdder u_4bitadder_2 (
    .A1(and_4_out), .B1(and_3_out), .A2(and_7_out), .B2(and_11_out), .A3(n4bitadder_1_out_10),
    .B3(n4bitadder_1_out_11), .A4(n4bitadder_1_out_12), .B4(n4bitadder_1_out_13), .out_10(out_13),
    .out_11(out_14), .out_12(out_15), .out_13(out_17), .out_9(out_18));
  and and_13 (and_13_out, A1, B1);
  and and_14 (and_14_out, A1, B2);
  and and_15 (and_15_out, A1, B3);
  and and_16 (out_16, B4, A1);
endmodule

module SignedMultiplier (
  input  A1,
  input  A2,
  input  A3,
  input  A4,
  input  B1,
  input  B2,
  input  B3,
  input  B4,
  output out_9,
  output out_10,
  output out_11,
  output out_12,
  output out_13,
  output out_14,
  output out_15,
  output out_16
);

  wire n4bitinverter_1_out_6, n4bitinverter_1_out_7, n4bitinverter_1_out_8, n4bitinverter_1_out_9,
       n4bitinverter_2_out_6, n4bitinverter_2_out_7, n4bitinverter_2_out_8, n4bitinverter_2_out_9, undriven,
       undriven_2, unsignedmultiplier_1_out_13, unsignedmultiplier_1_out_14, unsignedmultiplier_1_out_15,
       unsignedmultiplier_1_out_16, unsignedmultiplier_1_out_17, unsignedmultiplier_1_out_18,
       unsignedmultiplier_1_out_19, unsignedmultiplier_1_out_20, xor_1_out;

  xor xor_1 (xor_1_out, undriven, undriven_2);
  _4BitInverter u_4bitinverter_1 (
    .C(undriven), .A1(A1), .A2(A2), .in_3(A3), .A4(A4), .out_6(n4bitinverter_1_out_6),
    .out_7(n4bitinverter_1_out_7), .out_8(n4bitinverter_1_out_8), .out_9(n4bitinverter_1_out_9));
  UnsignedMultiplier unsignedmultiplier_1 (
    .C3(n4bitinverter_1_out_6), .C2(n4bitinverter_1_out_7), .C1(n4bitinverter_1_out_8),
    .in_8(n4bitinverter_1_out_9), .B1(n4bitinverter_2_out_6), .B2(n4bitinverter_2_out_7),
    .B3(n4bitinverter_2_out_8), .B4(n4bitinverter_2_out_9), .out_13(unsignedmultiplier_1_out_13),
    .out_14(unsignedmultiplier_1_out_14), .out_15(unsignedmultiplier_1_out_15),
    .out_17(unsignedmultiplier_1_out_17), .out_18(unsignedmultiplier_1_out_18),
    .out_19(unsignedmultiplier_1_out_19), .out_20(unsignedmultiplier_1_out_20),
    .out_16(unsignedmultiplier_1_out_16));  // open: A1, A2, A3, A4
  _8BitInverter u_8bitinverter_1 (
    .A1(unsignedmultiplier_1_out_16), .A2(unsignedmultiplier_1_out_20), .A3(unsignedmultiplier_1_out_19),
    .A4(unsignedmultiplier_1_out_18), .A5(unsignedmultiplier_1_out_17), .A6(unsignedmultiplier_1_out_15),
    .A7(unsignedmultiplier_1_out_14), .A8(unsignedmultiplier_1_out_13), .C(xor_1_out), .out_10(out_10),
    .out_11(out_12), .out_12(out_14), .out_13(out_16), .out_14(out_15), .out_15(out_13), .out_16(out_11),
    .out_17(out_9));
  _4BitInverter u_4bitinverter_2 (
    .C(undriven_2), .A1(B1), .A2(B2), .in_3(B3), .A4(B4), .out_6(n4bitinverter_2_out_6),
    .out_7(n4bitinverter_2_out_7), .out_8(n4bitinverter_2_out_8), .out_9(n4bitinverter_2_out_9));
endmodule
