// Logisim project AdderSubtractor.circ as structural Verilog: 1 circuit, main circuit main
module main (
  input  Adder_Subtractor,
  input  [4:0] in_2,
  input  [4:0] in_3,
  output [4:0] Out,
  output out_5
);

  wire [4:0] xor_1_out;

  Adder #(.width(5)) adder_1 (.a(in_2), .b(xor_1_out), .out(Out), .cin(Adder_Subtractor), .cout(out_5));
  xor xor_1 (xor_1_out[0], in_3[0], Adder_Subtractor);
  xor xor_2 (xor_1_out[1], in_3[1], Adder_Subtractor);
  xor xor_3 (xor_1_out[2], in_3[2], Adder_Subtractor);
  xor xor_4 (xor_1_out[3], in_3[3], Adder_Subtractor);
  xor xor_5 (xor_1_out[4], in_3[4], Adder_Subtractor);

  // Notes on the sheet:
  //   A
  //   B
  //   Adder/Subtractor - Subtractor uses Bitwise Controlled NOT 
endmodule
