// Logisim project CombinedDecoder.circ as structural Verilog: 1 circuit, main circuit main
module main (
  input  [2:0] in_1,
  output [7:0] _7_6_5_4_3_2_1_0,
  output _0,
  output _1,
  output _2,
  output _3,
  output _4,
  output _5,
  output _6,
  output _7
);

  wire not_1_out, not_2_out, not_3_out;

  not not_1 (not_1_out, in_1[2]);
  not not_2 (not_2_out, in_1[1]);
  not not_3 (not_3_out, in_1[0]);
  and and_1 (_0, not_1_out, not_2_out, not_3_out);
  and and_2 (_1, not_1_out, not_2_out, in_1[0]);
  and and_3 (_2, not_1_out, in_1[1], not_3_out);
  and and_4 (_3, not_1_out, in_1[1], in_1[0]);
  and and_5 (_4, in_1[2], not_2_out, not_3_out);
  and and_6 (_5, in_1[2], not_2_out, in_1[0]);
  and and_7 (_6, in_1[2], in_1[1], not_3_out);
  and and_8 (_7, in_1[2], in_1[1], in_1[0]);
  Decoder #(.select(3), .enable("false")) decoder_1 (
    .out0(_7_6_5_4_3_2_1_0[0]), .out1(_7_6_5_4_3_2_1_0[1]), .out2(_7_6_5_4_3_2_1_0[2]),
    .out3(_7_6_5_4_3_2_1_0[3]), .out4(_7_6_5_4_3_2_1_0[4]), .out5(_7_6_5_4_3_2_1_0[5]),
    .out6(_7_6_5_4_3_2_1_0[6]), .out7(_7_6_5_4_3_2_1_0[7]), .sel(in_1));

  // Notes on the sheet:
  //   3 to 8 Decoder
  //   3-bit Decoder which counts 0 to 7. The decoder uses NOT and AND gates. 
  //   Logisim Octal Decoder
  //   3-bit decoder which counts 0 to 7, using Logisim built-in Decoder Plexer
endmodule
