// Logisim project CombinedMultiplexer.circ as structural Verilog: 1 circuit, main circuit main
module main (
  input  in_1,
  input  [3:0] A,
  input  [3:0] B,
  output [3:0] out_4,
  output out_5,
  output out_6,
  output out_7,
  output out_8
);

  wire and_1_out, and_2_out, and_3_out, and_4_out, and_5_out, and_6_out, and_7_out, and_8_out, not_1_out;

  not not_1 (not_1_out, in_1);
  and and_1 (and_1_out, not_1_out, A[3]);
  and and_2 (and_2_out, not_1_out, A[2]);
  and and_3 (and_3_out, not_1_out, A[0]);
  and and_4 (and_4_out, not_1_out, A[1]);
  or or_1 (out_5, and_1_out, and_5_out);
  or or_2 (out_6, and_2_out, and_6_out);
  and and_5 (and_5_out, in_1, B[3]);
  and and_6 (and_6_out, in_1, B[2]);
  and and_7 (and_7_out, in_1, B[1]);
  or or_3 (out_7, and_4_out, and_7_out);
  or or_4 (out_8, and_3_out, and_8_out);
  and and_8 (and_8_out, in_1, B[0]);
  Multiplexer #(.width(4), .enable("false")) multiplexer_1 (.in0(A), .in1(B), .out(out_4), .sel(in_1));

  // Notes on the sheet:
  //   2 to 1 Multiplexer
  //   4-bit wide Multiplexer
  //   2 to 1 Multiplexer
  //   Multiplexer implemented using built-in Logisim module
endmodule
