// Logisim project FourBitFullAdder.circ as structural Verilog: 1 circuit, main circuit main
module main (
  input  Cin,
  input  A,
  input  B,
  input  A_2,
  input  B_2,
  input  A_3,
  input  B_3,
  input  A_4,
  input  B_4,
  output out_10,
  output out_11,
  output out_12,
  output out_13,
  output out_14
);

  wire CARRY_2_out, CARRY_3_out, CARRY_4_out, CARRY_5_out, CARRY_6_out, CARRY_7_out, CARRY_8_out, CARRY_out,
       Cout_3_out, Cout_4_out, Cout_out, SUM_2_out, SUM_3_out, SUM_4_out, SUM_out;

  xor SUM (SUM_out, A, B);
  and CARRY (CARRY_out, A, B);
  xor SUM_2 (SUM_2_out, A_2, B_2);
  and CARRY_2 (CARRY_2_out, A_2, B_2);
  xor SUM_3 (SUM_3_out, A_3, B_3);
  and CARRY_3 (CARRY_3_out, A_3, B_3);
  xor SUM_4 (SUM_4_out, A_4, B_4);
  and CARRY_4 (CARRY_4_out, A_4, B_4);
  xor SUM_5 (out_13, Cin, SUM_out);
  and CARRY_5 (CARRY_5_out, SUM_out, Cin);
  xor SUM_6 (out_12, Cout_3_out, SUM_2_out);
  and CARRY_6 (CARRY_6_out, SUM_2_out, Cout_3_out);
  xor Cout (Cout_out, CARRY_6_out, CARRY_2_out);
  xor SUM_7 (out_11, Cout_out, SUM_3_out);
  and CARRY_7 (CARRY_7_out, SUM_3_out, Cout_out);
  xor SUM_8 (out_10, Cout_4_out, SUM_4_out);
  and CARRY_8 (CARRY_8_out, SUM_4_out, Cout_4_out);
  xor Cout_2 (out_14, CARRY_8_out, CARRY_4_out);
  xor Cout_3 (Cout_3_out, CARRY_5_out, CARRY_out);
  xor Cout_4 (Cout_4_out, CARRY_7_out, CARRY_3_out);

  // Notes on the sheet:
  //   Four Bit Full Adder
  //   Combines four Full-Adders to make a four-bit full adder
endmodule
