// Logisim project OneBitHalfAdder.circ as structural Verilog: 1 circuit, main circuit main
module main (
  input  Cin,
  input  A,
  input  B,
  output out_4,
  output out_5
);

  wire CARRY_2_out, CARRY_out, SUM_out;

  xor SUM (SUM_out, A, B);
  and CARRY (CARRY_out, A, B);
  and CARRY_2 (CARRY_2_out, SUM_out, Cin);
  xor SUM_2 (out_4, Cin, SUM_out);
  xor Cout (out_5, CARRY_2_out, CARRY_out);

  // Notes on the sheet:
  //   FULL ADDER
  //   This Full-Adder adds three one-bit binary numbers (A B C) and outputs two on-bit binary numbers (SUM Cout)
endmodule
