// Logisim project SAMDatapath.circ as structural Verilog: 1 circuit, main circuit main
module main (
  output [7:0] Output_Display,
  output Pc,
  output Inc,
  output Amux,
  output Mar,
  output Mst,
  output Ir,
  output Dmux,
  output Acc,
  output Out,
  output Sub
);

  wire Add_out, and_2_out, and_6_out, and_7_out, clock_1_out, Clr_out, decoder_1_out2, decoder_1_out3,
       Hlt_out, Jaz_out, Jmp_out, Lda_out, not_1_out, or_2_out, or_4_out, or_5_out, Out_out, Sta_out, Sub_out;
  wire [1:0] counter_1_q;
  wire [3:0] multiplexer_1_out, not_2_out, PC_q, register_1_q, register_2_q;
  wire [7:0] adder_1_out, multiplexer_2_out, ram_1_data, register_3_q, xor_1_out;
  wire [7:4] register_2_q_2;

  Clock clock_1 (.out(clock_1_out));
  Button Clr (.out(Clr_out));
  and and_1 (Pc, or_5_out, decoder_1_out2);
  and and_2 (and_2_out, clock_1_out, Hlt_out);
  Counter #(.width(4), .max('hf)) u_PC (
    .load(Pc), .D(register_2_q), .count(Inc), .Q(PC_q), .clk(and_2_out), .clr(Clr_out));  // open: carry
  Counter #(.width(2), .max('h3)) counter_1 (
    .Q(counter_1_q), .clk(and_2_out), .clr(Clr_out));  // open: load, D, count, carry
  Decoder #(.select(2), .enable("false")) decoder_1 (
    .out0(Inc), .out1(Ir), .out2(decoder_1_out2), .out3(decoder_1_out3), .sel(counter_1_q));
  Multiplexer #(.width(4), .enable("false")) multiplexer_1 (
    .in0(PC_q), .in1(register_2_q), .out(multiplexer_1_out), .sel(Amux));
  and and_3 (Amux, or_4_out, decoder_1_out2);
  Register #(.width(4)) register_1 (.D(multiplexer_1_out), .en(Mar), .Q(register_1_q), .clk(and_2_out));  // open: clr
  or or_1 (Mar, Inc, or_4_out);
  and and_4 (Mst, decoder_1_out3, Sta_out);
  RAM #(.addrWidth(4), .bus("separate")) ram_1 (
    .addr(register_1_q), .din(register_3_q), .data(ram_1_data), .str(Mst), .clk(and_2_out));  // open: sel, ld, clr
  Register register_2 (.D(ram_1_data), .en(Ir), .Q({register_2_q_2, register_2_q}), .clk(and_2_out), .clr(Clr_out));
  and and_5 (Dmux, decoder_1_out3, Lda_out);
  or or_2 (or_2_out, register_3_q[7], register_3_q[6], register_3_q[5], register_3_q[4], register_3_q[3], register_3_q[2], register_3_q[1], register_3_q[0]);
  not not_1 (not_1_out, or_2_out);
  Register register_3 (.D(multiplexer_2_out), .en(Acc), .Q(register_3_q), .clk(and_2_out));  // open: clr
  Multiplexer #(.width(8), .enable("false")) multiplexer_2 (
    .in0(adder_1_out), .in1(ram_1_data), .out(multiplexer_2_out), .sel(Dmux));
  or or_3 (Acc, Dmux, Sub, and_6_out);
  and and_6 (and_6_out, decoder_1_out3, Add_out);
  or or_4 (or_4_out, Lda_out, Add_out, Sub_out, Sta_out);
  or or_5 (or_5_out, Jmp_out, and_7_out);
  and and_7 (and_7_out, not_1_out, Jaz_out);
  Register register_4 (.D(register_3_q), .en(Out), .Q(Output_Display), .clk(and_2_out));  // open: clr
  and and_8 (Sub, decoder_1_out3, Sub_out);
  and Lda (Lda_out, not_2_out[3], not_2_out[2], not_2_out[1], not_2_out[0]);
  and Add (Add_out, not_2_out[3], not_2_out[2], not_2_out[1], register_2_q_2[4]);
  and u_Sub (Sub_out, not_2_out[3], not_2_out[2], register_2_q_2[5], not_2_out[0]);
  and Sta (Sta_out, not_2_out[3], not_2_out[2], register_2_q_2[5], register_2_q_2[4]);
  and Jmp (Jmp_out, not_2_out[3], register_2_q_2[6], not_2_out[1], not_2_out[0]);
  and Jaz (Jaz_out, not_2_out[3], register_2_q_2[6], not_2_out[1], register_2_q_2[4]);
  and and_9 (Out, decoder_1_out2, Out_out);
  and u_Out (Out_out, register_2_q_2[7], register_2_q_2[6], register_2_q_2[5], not_2_out[0]);
  nand Hlt (Hlt_out, register_2_q_2[7], register_2_q_2[6], register_2_q_2[5], register_2_q_2[4]);
  assign xor_1_out = ram_1_data ^ {8{Sub}};  // XOR_Gate xor_1, 8 bits wide
  Adder adder_1 (.a(register_3_q), .b(xor_1_out), .out(adder_1_out), .cin(Sub));  // open: cout
  assign not_2_out = ~register_2_q_2;  // NOT_Gate not_2, 4 bits wide

  // Notes on the sheet:
  //   PC
  //   MAR
  //   SAM Datapath
  //   IR
  //   ACC
  //   OUT
endmodule
