// Logisim project TinyALU.circ as structural Verilog: 1 circuit, main circuit main
module main (
  input  [1:0] in_1,
  input  [3:0] in_2,
  output [3:0] out_3
);

  wire and_1_out, and_2_out, and_3_out, xor_1_out, xor_2_out, xor_3_out, xor_4_out;

  xor xor_1 (xor_1_out, in_2[0], in_1[1]);
  xor xor_2 (xor_2_out, in_2[1], in_1[1]);
  xor xor_3 (xor_3_out, in_2[2], in_1[1]);
  xor xor_4 (xor_4_out, in_2[3], in_1[1]);
  and and_1 (and_1_out, xor_1_out, in_1[0]);
  and and_2 (and_2_out, xor_2_out, and_1_out);
  and and_3 (and_3_out, xor_3_out, and_2_out);
  xor xor_5 (out_3[0], in_1[0], xor_1_out);
  xor xor_6 (out_3[1], and_1_out, xor_2_out);
  xor xor_7 (out_3[2], and_2_out, xor_3_out);
  xor xor_8 (out_3[3], and_3_out, xor_4_out);

  // Notes on the sheet:
  //   Tiny ALU which carries out logic operations.
  //   Tiny ALU
endmodule
