// Logisim project bitwisenot.circ as structural Verilog
module main (
  input  [4:0] in_1,
  input  in_2,
  output [4:0] out_3
);

  xor xor_1 (out_3[0], in_1[0], in_2);
  xor xor_2 (out_3[1], in_1[1], in_2);
  xor xor_3 (out_3[2], in_1[2], in_2);
  xor xor_4 (out_3[3], in_1[3], in_2);
  xor xor_5 (out_3[4], in_1[4], in_2);
endmodule
