// Logisim project Universal_Shift_Register_DFF.circ as structural Verilog: 1 circuit, main circuit main
module main (
  input  ShiftRight,
  input  I3,
  input  I2,
  input  I1,
  input  ShiftLeft,
  input  I0,
  input  [1:0] Selectors,
  output O3,
  output O2,
  output O1,
  output O0
);

  wire Clk_out, multiplexer_1_out, multiplexer_2_out, multiplexer_3_out, multiplexer_4_out;

  Multiplexer #(.select(2)) multiplexer_1 (
    .in0(O3), .in1(ShiftRight), .in2(O2), .in3(I3), .out(multiplexer_1_out), .sel(Selectors));
  Multiplexer #(.select(2)) multiplexer_2 (
    .in0(O2), .in1(O3), .in2(O1), .in3(I2), .out(multiplexer_2_out), .sel(Selectors));
  Multiplexer #(.select(2)) multiplexer_3 (
    .in0(O1), .in1(O2), .in2(O0), .in3(I1), .out(multiplexer_3_out), .sel(Selectors));
  Multiplexer #(.select(2)) multiplexer_4 (
    .in0(O0), .in1(O1), .in2(ShiftLeft), .in3(I0), .out(multiplexer_4_out), .sel(Selectors));
  D_Flip_Flop D3 (.D(multiplexer_1_out), .clk(Clk_out), .Q(O3));  // open: Qn, preset, reset
  D_Flip_Flop D2 (.D(multiplexer_2_out), .clk(Clk_out), .Q(O2));  // open: Qn, preset, reset
  D_Flip_Flop D1 (.D(multiplexer_3_out), .clk(Clk_out), .Q(O1));  // open: Qn, preset, reset
  D_Flip_Flop D0 (.D(multiplexer_4_out), .clk(Clk_out), .Q(O0));  // open: Qn, preset, reset
  Clock Clk (.out(Clk_out));

  // Notes on the sheet:
  //   Selector:
  //   0 0 Memory
  //   0 1 Shift Right
  //   1 0 Shift Left
  //   1 1 Parallel Load
  //   Universal Shift Register
  //   That is if the value O3, O2, O1, O0 are 1010 then,
  //   That is if the value O3, O2, O1, O0 are 1010 then,
  //   When selected it right shifts the value of the registers by adding the bit in ShiftRight in left
  //   For value of ShiftRight = 1, on 1 pass: 1101, 2 pass: 1110, 3 and further pass: 1111
  //   When selected it left shifts the value of the registers by adding the bit in ShiftLeft in right
  //   For value of ShiftLeft = 0, on 1 pass: 0100, 2 pass: 1000, 3 and further pass: 0000
  //   When selected it loads the value of I0, I1, I2, I3 in O0, O1, O2 and O3 respectively
  //   When selected it keeps the value of output pins O0, O1, etc. in there previous state and do not change them
  //   For value of ShiftRight = 0, on 1 pass: 0101, 2 pass: 0010, 3 pass: 0001, 4 and further pass: 0000
  //   For value of ShiftLeft = 1, on 1 pass: 0101, 2 pass: 1011, 3 pass: 0111, 4 and further pass: 1111
endmodule
